# Fritzing sketch Sketch (saved by Fritzing 0.9.3b)
circuit board: 8cm x 5.4cm

parts:
  Componente4 = Arduino Pro Mini v13
  Componente10 = GY-BMEP280 Barometric Pressure Sensor - Breakout
  Componente11 = XBee USB Mini Adapter
  VCC1 = Battery
  S2 = Toggle Switch [package=THT]
  R2 = Resistor [tolerance=±5% resistance=220 package="2010 [SMD]"]
  Componente9 = InvenSense MPU6050

nets (from the pcb view):
  VCC: Componente4.VCC, Componente10.VCC, Componente11.5V, Componente9.VCC
  GND: Componente4.GND, Componente10.GND, Componente11.GND, VCC1.-, Componente9.GND
  N1: Componente4.A4, Componente10.SDA, Componente9.SDA
  N2: Componente4.A5, Componente10.SCL, R2.Pin_1
  N3: Componente4.RAW, S2.COM
  N4: Componente4.D0/TX, Componente11.TXD
  N5: VCC1.+, S2.L2
  N6: R2.Pin_0, Componente9.SCL

custom parts:
  GY-BMEP280 Barometric Pressure Sensor - Breakout: The BME280 is a chip which was originally designed for the next generation of smartphones. It is made up of a very accurate pressure sensor and an associated temperature sensor which helps calibrate the pressure readings. And just for fun they threw in a pretty solid humidity sensor in there as well! So with an I2C connection you have access to enough weather data to make some pretty good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
