# Fritzing sketch Sketch Sensores Unidos (saved by Fritzing 0.9.3b)

parts:
  Componente4 = Arduino Pro Mini v13
  Componente6 = Bluetooth HC-05 Macho
  microSD2 = MicroSD Card Module
  J1 = female pin header, 2 pins [form="♀ (female)"]
  J2 = female pin header, 2 pins [form="♀ (female)"]
  U1 = LIPO-1000mAh [package=lipo-1000]
  Componente9 = GY 86
  SD_card_module1 = SD Card Module  # not connected

nets:
  N1: Componente4.A4, Componente9.SDA
  N2: Componente4.A5, Componente9.SCL
  N3: Componente4.RAW, U1.+
  N4: Componente4.GND, J2.pin1, U1.-
  N5: Componente4.VCC, J1.pin2
  N6: Componente4.D13/SCK, microSD2.MOSI
  N7: Componente4.D12/MISO, microSD2.VCC
  N8: Componente4.D11_PWM/MOSI, microSD2.MISO
  N9: Componente4.D4, Componente4.D3_PWM, microSD2.SCK
  N10: Componente4.D1/RX, Componente6.TXD
  N11: Componente4.D0/TX, Componente6.RXD
  N12: Componente6.VCC, J1.pin1, Componente9.VCC_IN
  GND: Componente6.GND, J2.pin2, Componente9.GND

notes:
  El sensor usador es el Gy-86, sin embargo en fritzing el mas parecido es el MPU6050
  Vcc-------->
  3.3v*------>
  gnd*------>
  scl*------->
  sda*------>
  *que tienen conexion
  Son dos baterias de 3.7v y 1100 mAh
  SDA->A4
  SCL->A5

custom parts:
  GY 86: The InvenSense MPU-6050 sensor contains a MEMS accelerometer and a MEMS gyro in a single chip. It is very accurate, as it contains 16-bits analog to digital conversion hardware for each channel. Therefor it captures the x, y, and z channel at the same time. The sensor uses the I2C-bus to interface with the Arduino.
  SD Card Module: SD Card Module Slot Socket Reader For Arduino ARM MCU
